# Fritzing sketch hackfest2015 (saved by Fritzing 0.9.2b)
perfboards: 14
breadboards: 1

parts:
  rp01 = Raspberry Pi 2
  ar01 = Arduino Mega 2560 (Rev3)
  casino_(lcd01) = 128 x 64 Graphic LCD
  LED2 = smd LED [color="Red (633nm)" package="0805 [SMD]"]
  R2 = Resistor [tolerance=±5% resistance=330 package=THT]
  ar02a = Arduino Uno (Rev3) - ICSP
  ar02b = Rotoshield - Motor driver shield for Arduino
  J1 = shrouded pin header, 10 pins [form="♂ (shrouded male)"]  # not connected
  5v = Power plug
  R3 = Photocell (LDR) [package=THT]
  R4 = Resistor [tolerance=±5% resistance=10k package="2512 [SMD]"]
  R1 = Resistor [tolerance=±5% resistance=10k package=THT]
  Q1 = Basic FET N-Channel [package="TO220 [THT]"]  # not connected
  5v1 = Power plug  # not connected
  LED3 = LED - 3mm [color="Red (633nm)" package="3 mm [THT]"]  # not connected
  LED4 = LED - 3mm [color="Red (633nm)" package="3 mm [THT]"]  # not connected
  LED5 = LED - 3mm [color="Red (633nm)" package="3 mm [THT]"]  # not connected
  LED6 = LED - 3mm [color="Red (633nm)" package="3 mm [THT]"]  # not connected
  LED7 = LED - 3mm [color="Red (633nm)" package="3 mm [THT]"]  # not connected
  fluidmotor01_(12v) = Plastic Solenoid Valve  # not connected
  solenoid01_(12v) = Plastic Solenoid Valve  # not connected
  flowmeter01 = Plastic Solenoid Valve  # not connected
  U1 = LCD-16X2 [package=lcd-16x2]
  R5 = Resistor [tolerance=±5% resistance=330 package=THT]
  R6 = Resistor [tolerance=±5% resistance=330 package=THT]  # not connected
  X1 = USB Connectors [package=usb-a-s]  # not connected

nets:
  N1: rp01.GPIO2, ar01.D20/SDA
  N2: rp01.GPIO3, ar01.D21/SCL
  N3: rp01.GIPO10, ar02a.D11_PWM/MOSI
  N4: rp01.GIPO9, ar02a.D12/MISO
  N5: rp01.GIPO11, ar02a.D13/SCK
  GND: rp01.GND, ar01.GND, casino_(lcd01).1_Vss, casino_(lcd01).15_CS1, casino_(lcd01).20_K(-), ar02a.GND, ar02b.GND, 5v.GND, R4.Pin_0, U1.VSS
  N6: rp01.GIPO8, ar02a.D10_PWM/SS
  N7: ar01.D13_PWM, casino_(lcd01).6_Enable
  N8: ar01.D12_PWM, casino_(lcd01).5_R/W
  N9: ar01.D11_PWM, casino_(lcd01).4_D/I
  N10: ar01.D10_PWM, casino_(lcd01).3_Vo
  N11: ar01.D8_PWM, R2.Pin_1
  N12: ar01.D2_PWM, U1.DB7
  N13: ar01.D3_PWM, U1.DB6
  N14: ar01.D4_PWM, U1.DB5
  N15: ar01.D5_PWM, U1.DB4
  N16: ar01.D6_PWM, U1.E
  N17: ar01.D7_PWM, U1.RS
  VCC: casino_(lcd01).2_Vdd, ar02b.VCC, 5v.VCC, R3.pin_1, R1.Pin_1, U1.VDD, R5.Pin_1
  N18: LED2.anode, R2.Pin_0
  N19: ar02a.A0, R3.pin_0, R4.Pin_1
  N20: U1.R_W, U1.K
